# Fritzing sketch wiring_diagram (saved by Fritzing 0.9.10b)
perfboards: 1

parts:
  Grove1 = Grove 4 Digit Display
  RE1 = Rotary Encoder [package=THT]
  S1 = Pushbutton [package="[SMD]"]
  S2 = Pushbutton [package="[THT]"]
  RE2 = Rotary Encoder [package=THT]
  Part1 = Arduino Nano (Rev3.0)
  Part2 = PN532 Elechouse RFID NFC Module V3
  S3 = D2F-FL Omron Snap Action Limit Switch with Level
  M1 = sv5w
  SP1 = SPEAKER [package=pcb_mount_speaker]
  A1 = SM5308 battery charger module
  U1 = LIPO-110mAh [package=lipo-110]

nets:
  GND: Grove1.GND, RE1.EncoderPinC, S1.Pin_1, S1.Pin_2, S2.Pin_3, S2.Pin_4, RE2.EncoderPinC, Part1.GND, Part2.GND, S3.Pin_1, M1.GND, M1.GND-12
  VCC: Grove1.VCC, Part1.5V, Part2.VCC, M1.VCC, A1.Pin_4
  N1: Grove1.DIO, Part1.D11/MOSI
  N2: Grove1.CLK, Part1.D10
  N3: RE1.EncoderPinA, Part1.D3
  N4: RE1.EncoderPinB, Part1.D4
  N5: S1.Pin_3, S1.Pin_4, Part1.D2
  N6: S2.Pin_1, S2.Pin_2, Part1.D5
  N7: RE2.EncoderPinA, Part1.D6
  N8: RE2.EncoderPinB, Part1.D7
  N9: Part1.D9, Part2.A10
  N10: Part1.D12/MISO, M1.TXD/IO0
  N11: Part1.A5, Part2.SCL
  N12: Part1.A4, Part2.SDA
  N13: Part1.A3, S3.Pin_3
  N14: Part1.D13/SCK, M1.RXD/IO1
  N15: S3.Pin_2, A1.Pin_1, A1.Pin_5, U1.-
  N16: M1.Spk-, SP1.+
  N17: M1.Spk+, SP1.-
  N18: A1.Pin_2, U1.+

custom parts:
  PN532 Elechouse RFID NFC Module V3: NFC is a popular technology in recent years. We often heard this work while smart phone company such as Samsung or HTC introduces their latest high-end phones. Almost all the high-end phone in the market support NFC. Near field communication (NFC) is a set of standards for smart phones and similar devices to establish radio communication with each other by touching them together or bringing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
  D2F-FL Omron Snap Action Limit Switch with Level: Snap action switch with stainless steel lever.
  sv5w: DY-SV5W is an intelligent voice module. It integrates I/O subsection triggering, UART serial port control, ONE_line single bus serial port control3. Onboard 5W Class D amplifier circuit and can directly drive 4ohm 3~5W speakers. Support MP3,WAV decoding format. Max support 32Gbit(4MByte) TF card memory, can connect the computer to update TF card to store audio files via USB cable.
  SM5308 battery charger module: Charger module for Lipo Battery from Usb, 5v 2a, Sm5308 chip.
